# Fritzing sketch accessories_pcb (saved by Fritzing 0.9.3b)
circuit board: 9.41637cm x 4.35586cm
breadboards: 1

parts:
  J = 4 pins header [package=THT]
  Encoder = Rotary Encoder with Switch [package=THT]
  J_2 = 4 pins header [package=THT]
  J_3 = 4 pins header [package=THT]
  J_4 = 4 pins header [package=THT]
  Encoder_2 = Rotary Encoder with Switch [package=THT]
  J_5 = 4 pins header [package=THT]
  J_6 = 4 pins header [package=THT]
  Encoder_3 = Rotary Encoder with Switch [package=THT]
  Encoder_4 = Rotary Encoder with Switch [package=THT]
  Power = PowerButton [package="[THT]"]
  Power_2 = PowerButton [package="[THT]"]

nets:
  N1: J.Pin_1, Encoder.EncoderPinA
  N2: J.Pin_2, Encoder.CommonPinC, Encoder.Switch_Pin_1
  N3: J.Pin_3, Encoder.EncoderPinB
  N4: J.Pin_4, Encoder.Switch_pin_2
  N5: J_2.Pin_1, Power.pin_5
  N6: J_2.Pin_2, Power.Pin_3, Power.pin_4, Power.pin_6
  N7: J_2.Pin_3, Power.Pin_1, Power.Pin_2
  N8: J_3.Pin_1, Power_2.pin_5
  N9: J_3.Pin_2, Power_2.Pin_3, Power_2.pin_4, Power_2.pin_6
  N10: J_3.Pin_3, Power_2.Pin_1, Power_2.Pin_2
  N11: J_4.Pin_1, Encoder_2.EncoderPinA
  N12: J_4.Pin_2, Encoder_2.CommonPinC, Encoder_2.Switch_Pin_1
  N13: J_4.Pin_3, Encoder_2.EncoderPinB
  N14: J_4.Pin_4, Encoder_2.Switch_pin_2
  N15: J_5.Pin_1, Encoder_3.EncoderPinA
  N16: J_5.Pin_2, Encoder_3.CommonPinC, Encoder_3.Switch_Pin_1
  N17: J_5.Pin_3, Encoder_3.EncoderPinB
  N18: J_5.Pin_4, Encoder_3.Switch_pin_2
  N19: J_6.Pin_1, Encoder_4.EncoderPinA
  N20: J_6.Pin_2, Encoder_4.CommonPinC, Encoder_4.Switch_Pin_1
  N21: J_6.Pin_3, Encoder_4.EncoderPinB
  N22: J_6.Pin_4, Encoder_4.Switch_pin_2

notes:
  PinA
  Gnd
  PinB
  Sw
  Led

custom parts:
  4 pins header: 4 pins header, drawn from Stephen Parry
  Rotary Encoder with Switch: Extended from Rotary Encoder from ALPS STEC12E07. Fabian Althaus
  PowerButton: A power button : a push button with a led
