# Fritzing sketch Accessoires (saved by Fritzing 0.9.3b)
circuit board: 9.41637cm x 4.35586cm
breadboards: 1

parts:
  J1 = 4 pins header [package=THT]
  RES1 = Rotary Encoder with Switch [package=THT]
  S1 = PowerButton [package="[THT]"]
  J2 = 4 pins header [package=THT]
  S3 = PowerButton [package="[THT]"]
  J5 = 4 pins header [package=THT]
  J6 = 4 pins header [package=THT]
  RES2 = Rotary Encoder with Switch [package=THT]
  J7 = 4 pins header [package=THT]
  J8 = 4 pins header [package=THT]
  RES3 = Rotary Encoder with Switch [package=THT]
  RES4 = Rotary Encoder with Switch [package=THT]

nets:
  N1: J1.Pin_1, RES1.EncoderPinA
  N2: J1.Pin_2, RES1.CommonPinC, RES1.Switch_Pin_1
  N3: J1.Pin_3, RES1.EncoderPinB
  N4: J1.Pin_4, RES1.Switch_pin_2
  N5: S1.Pin_1, S1.Pin_2, J2.Pin_3
  N6: S1.Pin_3, S1.pin_4, S1.pin_6, J2.Pin_2
  N7: S1.pin_5, J2.Pin_1
  N8: S3.Pin_1, S3.Pin_2, J5.Pin_3
  N9: S3.Pin_3, S3.pin_4, S3.pin_6, J5.Pin_2
  N10: S3.pin_5, J5.Pin_1
  N11: J6.Pin_1, RES2.EncoderPinA
  N12: J6.Pin_2, RES2.CommonPinC, RES2.Switch_Pin_1
  N13: J6.Pin_3, RES2.EncoderPinB
  N14: J6.Pin_4, RES2.Switch_pin_2
  N15: J7.Pin_1, RES3.EncoderPinA
  N16: J7.Pin_2, RES3.CommonPinC, RES3.Switch_Pin_1
  N17: J7.Pin_3, RES3.EncoderPinB
  N18: J7.Pin_4, RES3.Switch_pin_2
  N19: J8.Pin_1, RES4.EncoderPinA
  N20: J8.Pin_2, RES4.CommonPinC, RES4.Switch_Pin_1
  N21: J8.Pin_3, RES4.EncoderPinB
  N22: J8.Pin_4, RES4.Switch_pin_2

custom parts:
  4 pins header: 4 pins header, drawn from Stephen Parry
  Rotary Encoder with Switch: Extended from Rotary Encoder from ALPS STEC12E07. Fabian Althaus
  PowerButton: A power button : a push button with a led
