# Fritzing sketch sketch_for_parts (saved by Fritzing 0.9.3b)
circuit board: 8.46667cm x 5.64444cm
breadboards: 1

parts:
  J2 = JST-B3P-VH [part_number=JST-B3P-VH package=THT]
  JP2 = Header 4 [package=molex-1x4_lock]
  J3 = JST-B3P-VH [part_number=JST-B3P-VH package=THT]  # not connected
  J5 = JST-B3P-VH [part_number=JST-B3P-VH package=THT]
  J5_2 = JST-B3P-VH [part_number=JST-B3P-VH package=THT]
  J5_3 = JST-VHR-3N [part_number=JST-VHR-3N package=THT]
  RE1 = Rotary Encoder [package=THT]  # not connected
  J4 = KF2510-4P [part_number=KF2510-4P package=THT]  # not connected
  J6 = KF2510-4P [part_number=KF2510-4P package=THT]
  U1 = ENCODER_2LED [package=encoder_led_2]  # not connected
  SW1 = ENCODER_RGB_CA [package=encoder_led_3]  # not connected

nets (from the pcb view):
  N1: J2.pin1, J6.pin1
  N2: JP2.1, J5.pin_4
  N3: JP2.2, J5.pin3, J5_2.pin3, J5_3.pin3, J5_3.pin_6, J6.pin4
  N4: JP2.3, J5.pin2, J5_2.pin2, J5_3.pin2, J5_3.pin_5
  N5: JP2.4, J5.pin1, J5_2.pin1, J5_3.pin1, J5_3.pin_4

custom parts:
  JST-B3P-VH: JST-B3P-VH Male 3 pin header from JST VH series. The female partner connector (JST-VHR-3N) to this is used on Dagu motors in their robots. This part is not breadboard or stripboard friendly - the pin spacings are not properly compatible. However, you can make the part fit by drilling between the tracks for the outer connectors and soldering a trace across them. This can be represented in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
  JST-B3P-VH: JST-B3P-VH Male 3 pin header from JST VH series. The female partner connector (JST-VHR-3N) to this is used on Dagu motors in their robots. This part is not breadboard or stripboard friendly - the pin spacings are not properly compatible. However, you can make the part fit by drilling between the tracks for the outer connectors and soldering a trace across them. This can be represented in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
  KF2510-4P: KF2510-4P Male 4 pin header. When plugging the female connector onto this, ensure that the correct connectors on the female part is located on the correct connector on the male part.
