# Fritzing sketch webradio_pcb (saved by Fritzing 0.9.3b)
circuit board: 10.0085cm x 3.15cm
breadboards: 1

parts:
  Logic_level_converter = Logic Level Converter
  R1 = Resistor [tolerance=±5% resistance=330 package=THT]
  Volume = KF2510-4P [part_number=KF2510-4P package=THT]
  Power = KF2510-4P [part_number=KF2510-4P package=THT]
  Station = KF2510-4P [part_number=KF2510-4P package=THT]
  LCD = KF2510-4P [part_number=KF2510-4P package=THT]
  Raspberry_Pi_Zero_W = Raspberry Pi Zero

nets:
  N1: Logic_level_converter.TX2_LV, Raspberry_Pi_Zero_W.pin_3
  N2: Logic_level_converter.RX2_LV, Raspberry_Pi_Zero_W.pin_5
  N3: Logic_level_converter.GND, Volume.pin2, Power.pin2, Station.pin2, LCD.pin1, Raspberry_Pi_Zero_W.pin_6, Raspberry_Pi_Zero_W.pin_9, Raspberry_Pi_Zero_W.pin_25, Raspberry_Pi_Zero_W.pin_39
  N4: Logic_level_converter.LV, Raspberry_Pi_Zero_W.pin_1, Raspberry_Pi_Zero_W.pin_17
  N5: Logic_level_converter.HV, LCD.pin2, Raspberry_Pi_Zero_W.pin_2
  N6: Logic_level_converter.RX2_HV, LCD.pin4
  N7: Logic_level_converter.TX2_HV, LCD.pin3
  N8: R1.Pin_0, Raspberry_Pi_Zero_W.pin_33
  N9: R1.Pin_1, Power.pin1
  N10: Volume.pin1, Raspberry_Pi_Zero_W.pin_31
  N11: Volume.pin3, Raspberry_Pi_Zero_W.pin_29
  N12: Volume.pin4, Raspberry_Pi_Zero_W.pin_23
  N13: Power.pin3, Raspberry_Pi_Zero_W.pin_32
  N14: Station.pin1, Raspberry_Pi_Zero_W.pin_7
  N15: Station.pin3, Raspberry_Pi_Zero_W.pin_13
  N16: Station.pin4, Raspberry_Pi_Zero_W.pin_11

notes:
  Sebastien ROY
  Gnd
  Vcc
  PinA
  PinB
  Sw
  Da
  Cl
  Led
  Webradio
  1
  39

custom parts:
  KF2510-4P: KF2510-4P Male 4 pin header. When plugging the female connector onto this, ensure that the correct connectors on the female part is located on the correct connector on the male part.

// code stored in the sketch: webradio.ino
kf
